# Fritzing sketch FED Schematic (saved by Fritzing 0.9.1b)
breadboards: 1

parts:
  IC1 = L293D [package=THT]
  Part2 = Arduino Wireless SD Shield
  U1 = 7-SEGMENT-4DIGIT [package=7-segment-4digit]
  MOTOR1 = Adafruit Gear-Reduced Stepper Motor (small)
  PI = TSOP312.., 314.. [package=THT]
  S1 = Momentary Switch [package=ksa_sealed_tac_switch]
  LED1 = LEDs [package=led10mm]
  U2 = BATTERY-2 [package=battery-aaa]

nets:
  N1: IC1.Enable_1, Part2.D8
  N2: IC1.In_1, Part2.D7
  N3: IC1.Out_1_(_Controlled_by_Enable_1_), MOTOR1.BLUE
  N4: IC1.0V, Part2.GND, S1.3, LED1.A, U2.+1
  N5: IC1.Out_2_(_Controlled_by_Enable_1_), MOTOR1.YELLOW
  N6: IC1.In_2, Part2.D6
  N7: IC1.+Vmotor, IC1.+V, Part2.+5V
  N8: IC1.Enable_2, Part2.D11
  N9: IC1.In_3, Part2.D5
  N10: IC1.Out_3_(_Controlled_by_Enable_2_), MOTOR1.PINK
  N11: IC1.Out_4_(_Controlled_by_Enable_2_), MOTOR1.ORANGE
  N12: IC1.In_4, Part2.SD_CS
  N13: Part2.D9, U1.1
  N14: Part2.D2, PI.Data
  N15: Part2.D3, LED1.C
  N16: Part2.3.3V, U1.7
  N17: Part2.VIN, S1.2
  N18: S1.4, U2.-1

custom parts:
  Adafruit Gear-Reduced Stepper Motor (small): Adafruit gear-reduction stepper motor (small)
